# Fritzing sketch F1 (saved by Fritzing 0.8.7b)
circuit board: 8.46667cm x 5.64444cm
breadboards: 1

parts:
  CuSensor = ACS712 Low Current Sensor Board v12
  U1 = RELAY [package=relay-g5q]
  Q1 = NPN-Transistor [package="TO92 [THT]"]
  D1 = Diode [package=diode-1n4001]
  R1 = Resistor [tolerance=±5% resistance=220 package=THT]
  U2 = ESP8266 WiFi Module [part_number=ESP8266]
  R2 = Resistor [tolerance=±5% resistance=220 package=THT]
  R3 = Resistor [tolerance=±5% resistance=220 package=THT]
  load = Screw terminal - 2 pins [package=THT]
  5v_DC = Screw terminal - 2 pins [package=THT]
  Home_Power = Screw terminal - 2 pins [package=THT]

nets:
  N1: CuSensor.IP+, Home_Power.pin1
  N2: CuSensor.IP-, load.pin1
  5V: CuSensor.5V, U1.COIL2, D1.C, U2.VCC, 5v_DC.pin1
  N3: CuSensor.VO, R2.Pin_0
  GND: CuSensor.GND, Q1.E, U2.GND, R3.Pin_1, 5v_DC.pin2
  N4: U1.MAIN, load.pin2
  N5: U1.NO, Home_Power.pin2
  N6: U1.COIL1, Q1.C, D1.A
  N7: Q1.B, R1.Pin_1
  N8: R1.Pin_0, U2.GPIO_5
  N9: U2.ADC_0, R2.Pin_1, R3.Pin_0

notes:
  1- ESP Devkit, has builtin regulator.
  2- we choose 5v Relay. 3- resistors value are not real.
  4- there must be a terminals for home power plug, load, and 5v DC

custom parts:
  ESP8266 WiFi Module: Generic WiFi Module based on the ESP8266 with onboard PCB antenna and UART communications
